# Fritzing sketch project (saved by Fritzing 0.9.3b)
circuit board: 8.46667cm x 5.64444cm
breadboards: 1

parts:
  Q1 = Basic FET P-Channel [package="TO220 [THT]"]
  Q2 = Basic FET P-Channel [package="TO220 [THT]"]
  Q3 = Basic FET P-Channel [package="TO220 [THT]"]
  DIN1 = DIN-5 jack (MIDI) [package=THT]
  Part1 = Arduino Nano (Rev3.0)
  J1 = Power Jack [package=power_jack_pth_lock]

nets:
  N1: Q1.gate, Part1.D6
  N2: Q1.drain, DIN1.1
  GND: Q1.source, Q2.source, Q3.source, Part1.GND, J1.GND
  N3: Q2.gate, Part1.D5
  N4: Q2.drain, DIN1.2
  N5: Q3.gate, Part1.D3
  N6: Q3.drain, DIN1.3
  N7: DIN1.4, Part1.VIN, J1.PWR

notes:
  12V 1A Center Positive
  Racing Ring Lighting Controller, 1.0
